# Fritzing sketch Prototype Schematic (saved by Fritzing 1.0.5)

parts:
  Part1 = 16-Channel 12-bit PCA9685 PWM/Servo Driver
  Part3 = Arduino Uno (Rev3) - ICSP
  J1 = Basic Servo
  R1 = Rotary Potentiometer (Small) [maximum_resistance=10kΩ knob_status=50% power=0.5W package=THT]
  R2 = Rotary Potentiometer (Small) [maximum_resistance=10kΩ knob_status=50% power=0.5W package=THT]
  R3 = Rotary Potentiometer (Small) [maximum_resistance=10kΩ knob_status=50% power=0.5W package=THT]
  R4 = Rotary Potentiometer (Small) [maximum_resistance=10kΩ knob_status=50% power=0.5W package=THT]
  S2 = Pushbutton [package="[THT]"]
  J2 = Basic Servo
  J3 = Basic Servo
  J4 = Basic Servo
  Power_plug1 = Power plug

nets:
  N1: Part1.PWRIN, Power_plug1.VCC
  GND: Part1.GND, J1.gnd, R1.leg2, R2.leg2, R3.leg2, R4.leg2, S2.Pin_3, S2.Pin_4, J2.gnd, J3.gnd, J4.gnd, Power_plug1.GND
  VCC: Part1.V+, Part3.VIN, J1.vcc, J2.vcc, J3.vcc, J4.vcc
  VCC_2: Part1.VCC, Part3.5V, R1.leg1, R2.leg1, R3.leg1, R4.leg1
  N2: Part1.SDA, Part3.A4/SDA
  N3: Part1.SCL, Part3.A5/SCL
  N4: Part1.12, J1.pulse
  N5: Part1.13, J2.pulse
  N6: Part1.14, J4.pulse
  N7: Part1.15, J3.pulse
  N8: Part3.A0, R4.wiper
  N9: Part3.A1, R3.wiper
  N10: Part3.A2, R2.wiper
  N11: Part3.A3, R1.wiper
  N12: Part3.ICSP_SCK, Part3.D13/SCK, S2.Pin_1

notes:
  *Pots should be wired in parallel

custom parts:
  16-Channel 12-bit PCA9685 PWM/Servo Driver: The Adafruit 16-Channel 12-bit PWM/Servo Driver will drive up to 16 servos over I2C with only 2 pins. The on-board PCA9685 PWM controller will drive all 16 channels simultaneously with no additional processing overhead. What's more, you can chain up to 62 of them to control up to 992 servos - all with the same 2 pins
